// Logisim project alu.circ as structural Verilog
module main (
  input  [31:0] X,
  input  [31:0] Y,
  input  Clock,
  input  Mul_Div_Reset,
  input  [5:0] Switch__S,
  output Equal,
  output Signed_Overflow,
  output [31:0] RESULT,
  output [31:0] toHi,
  output Stall_Pipeline
);

  wire add_cmd, add_overflow, and_1_out, comparator_1_lt, comparator_2_lt, comparator_3_eq, div, mul,
       multiplexer_4_out, multiplexer_5_out, or_1_out, or_2_out, overflow_add, overflow_sub, stall, stall_1,
       stall_div, stall_eq_ctr, stall_mul, sub_cmd, sub_overflow;
  wire [4:0] funct_mux, funct_reg, shift;
  wire [31:0] _16, _18, _20_out, _21_out, _30, _31, adder_1_out, bit_extender_1_out, bit_extender_2_out,
       counter_1_q, counter_2_q, HI, shifter_1_out, shifter_2_out, shifter_3_out, subtractor_1_out,
       subtractor_2_out;

  // Probe on X
  // Probe on Y
  BitSelector #(.width(32), .group(5)) bitselector_1 (.in(Y), .out(shift), .sel(3'b000));
  Register #(.width(5)) register_1 (
    .D({Switch__S[5], Switch__S[3:0]}), .en(Mul_Div_Reset), .Q(funct_reg), .clk(Clock));  // open: clr
  Multiplexer #(.width(5)) multiplexer_1 (
    .in0({Switch__S[5], Switch__S[3:0]}), .in1(funct_reg), .out(funct_mux), .sel(or_1_out));  // open: en
  or or_1 (or_1_out, stall, stall_1);
  ADD add_1 (.X(X), .Y(Y), .add_16(_16), .Overflow(add_overflow));
  SUB sub_1 (.X(X), .add_16(_18), .Y(Y), .Overflow(sub_overflow));
  MULAD mulad_1 (.X(X), .Y(Y), .Clock(Clock), .Mul_Div_Reset(Mul_Div_Reset), .Product(_30), .Stall_Pipeline(stall_mul));
  DIVSUB divsub_1 (
    .X(X), .Y(Y), .Clock(Clock), .Mul_Div_Reset(Mul_Div_Reset), .Stall_Pipeline(stall_div), .toHi(HI),
    .Division(_31));
  Shifter #(.width(32)) shifter_1 (.in(X), .\dist (shift), .out(shifter_1_out));
  Shifter #(.width(32), .shift("lr")) shifter_2 (.in(X), .\dist (shift), .out(shifter_2_out));
  Shifter #(.width(32), .shift("ar")) shifter_3 (.in(X), .\dist (shift), .out(shifter_3_out));
  Adder #(.width(32)) adder_1 (.a(X), .b(Y), .out(adder_1_out));  // open: cin, cout
  Subtractor #(.width(32)) subtractor_1 (.a(X), .b(Y), .out(subtractor_1_out));  // open: bin, bout
  assign _20_out = X & Y;  // AND_Gate _20, 32 bits wide
  assign _21_out = X | Y;  // OR_Gate _21, 32 bits wide
  Comparator #(.width(32)) comparator_1 (.a(X), .b(Y), .eq(Equal), .lt(comparator_1_lt));  // open: gt
  Comparator #(.width(32), .mode("unsigned")) comparator_2 (
    .a(X), .b(Y), .eq(Equal), .lt(comparator_2_lt));  // open: gt
  // Probe on counter_1_q
  Counter #(.width(32), .max('hffffffff)) counter_1 (
    .count(stall), .Q(counter_1_q), .clk(Clock), .clr(Mul_Div_Reset));  // open: load, D, carry
  Counter #(.width(32), .max('hffffffff)) counter_2 (
    .Q(counter_2_q), .clk(Clock), .clr(Mul_Div_Reset));  // open: load, D, count, carry
  and and_1 (and_1_out, stall_eq_ctr, or_2_out);
  or or_2 (or_2_out, mul, div);
  Comparator #(.width(1)) comparator_3 (.a(stall), .b(1'b0), .eq(comparator_3_eq));  // open: gt, lt
  assign bit_extender_1_out = {{31{1'b0}}, comparator_1_lt};  // Bit_Extender bit_extender_1
  assign bit_extender_2_out = {{31{1'b0}}, comparator_2_lt};  // Bit_Extender bit_extender_2
  Subtractor #(.width(32)) subtractor_2 (.a(counter_1_q), .b(counter_2_q), .out(subtractor_2_out));  // open: bin, bout
  // Probe on subtractor_2_out
  and and_2 (stall_1, and_1_out, comparator_3_eq);
  Multiplexer #(.select(5), .width(32)) multiplexer_2 (
    .in0(shifter_1_out), .in2(shifter_2_out), .in3(shifter_3_out), .in16(_16), .in17(adder_1_out),
    .in18(_18), .in19(subtractor_1_out), .in20(_20_out), .in21(_21_out), .in26(bit_extender_1_out),
    .in27(bit_extender_2_out), .in30(_30), .in31(_31), .out(RESULT), .sel(funct_mux));  // open: in1, in4, in5, in6, in7, in8, in9, in10, in11, in12, in13, in14, in15, in22, in23, in24, in25, in28, in29, en
  Comparator #(.width(32)) comparator_4 (.a(subtractor_2_out), .b({32{1'b0}}), .eq(stall_eq_ctr));  // open: gt, lt
  // Probe on funct_mux
  Multiplexer #(.width(32)) multiplexer_3 (.in0({32{1'b0}}), .in1(HI), .out(toHi), .sel(div));  // open: en
  // Probe on RESULT
  Multiplexer multiplexer_4 (.in0(1'b0), .in1(stall_mul), .out(multiplexer_4_out), .sel(mul));  // open: en
  Multiplexer multiplexer_5 (.in0(1'b0), .in1(stall_div), .out(multiplexer_5_out), .sel(div));  // open: en
  or or_3 (Stall_Pipeline, stall, Mul_Div_Reset);
  Comparator #(.width(5)) comparator_5 (.a(funct_reg), .b(5'b11110), .eq(mul));  // open: gt, lt
  Comparator #(.width(5)) comparator_6 (.a(funct_reg), .b({5{1'b1}}), .eq(div));  // open: gt, lt
  or or_4 (stall, multiplexer_4_out, multiplexer_5_out);
  // Probe on add_cmd
  Comparator #(.width(6), .mode("unsigned")) comparator_7 (.a(6'b100000), .b(Switch__S), .eq(add_cmd));  // open: gt, lt
  // Probe on sub_cmd
  Comparator #(.width(6), .mode("unsigned")) comparator_8 (.a(6'b100010), .b(Switch__S), .eq(sub_cmd));  // open: gt, lt
  or or_5 (Signed_Overflow, overflow_add, overflow_sub);
  Multiplexer multiplexer_6 (.in0(1'b0), .in1(add_overflow), .out(overflow_add), .sel(add_cmd));  // open: en
  Multiplexer multiplexer_7 (.in0(1'b0), .in1(sub_overflow), .out(overflow_sub), .sel(sub_cmd));  // open: en

  // Other names for the same wires on the sheet: clk = Clock; eq = Equal; funct[4:0] = {Switch__S[5], Switch__S[3:0]};
  //   s[5:0] = Switch__S; overflow = Signed_Overflow; rst = Mul_Div_Reset; val[31:0] = RESULT

  // Notes on the sheet:
  //   INPUTS to your circuit
  //   INPUT to your circuit
  //   DON'T CHANGE THE INPUTS AND OUTPUTS! IF YOU DO SO, YOU NEED TO MAKE SURE THE PINS ARE IN THE RIGHT PLACES!
  //   OUTPUTS of your circuit
endmodule

// 16
module ADD (
  input  [31:0] X,
  input  [31:0] Y,
  output [31:0] add_16,
  output Overflow
);

  wire carry_in, carry_out;
  wire [30:0] adder_2_out;

  // Probe on carry_out
  Adder #(.width(32)) adder_1 (.a(X), .b(Y), .out(add_16), .cout(carry_out));  // open: cin
  Adder #(.width(32)) adder_2 (
    .a({1'b0, X[30:0]}), .b({1'b0, Y[30:0]}), .out({carry_in, adder_2_out}));  // open: cin, cout
  // Probe on {1'b0, X[30:0]}
  // Probe on {1'b0, Y[30:0]}
  // Probe on Overflow
  xor xor_1 (Overflow, carry_in, carry_out);

  // Other names for the same wires on the sheet: add_out[31:0] = add_16; x_prime[30:0] = X[30:0];
  //   y_prime[30:0] = Y[30:0]
endmodule

// 18
module SUB (
  input  [31:0] X,
  input  [31:0] Y,
  output [31:0] add_16,
  output Overflow
);

  wire carry_in, carry_out;
  wire [30:0] subtractor_2_out;

  // Probe on carry_out
  Subtractor #(.width(32)) subtractor_1 (.a(X), .b(Y), .out(add_16), .bout(carry_out));  // open: bin
  Subtractor #(.width(32)) subtractor_2 (
    .a({1'b0, X[30:0]}), .b({1'b0, Y[30:0]}), .out({carry_in, subtractor_2_out}));  // open: bin, bout
  // Probe on {1'b0, X[30:0]}
  // Probe on {1'b0, Y[30:0]}
  // Probe on Overflow
  xor xor_1 (Overflow, carry_in, carry_out);

  // Other names for the same wires on the sheet: add_out[31:0] = add_16; x_prime[30:0] = X[30:0];
  //   y_prime[30:0] = Y[30:0]
endmodule

// 30
module MULAD (
  input  [31:0] X,
  input  [31:0] Y,
  input  Clock,
  input  Mul_Div_Reset,
  output [31:0] Product,
  output Stall_Pipeline
);

  wire shouldStall1, shouldStall2;
  wire [31:0] ctr, multiplexer_1_out, prev_val, register_1_q, y_reg;

  Register #(.width(32)) register_1 (.D(X), .en(Mul_Div_Reset), .Q(register_1_q), .clk(Clock));  // open: clr
  Register #(.width(32)) register_2 (.D(Y), .en(Mul_Div_Reset), .Q(y_reg), .clk(Clock));  // open: clr
  Counter #(.width(32), .max('hffffffff)) counter_1 (
    .Q(ctr), .clk(Clock), .clr(Mul_Div_Reset));  // open: load, D, count, carry
  Multiplexer #(.width(32)) multiplexer_1 (
    .in0({32{1'b0}}), .in1(register_1_q), .out(multiplexer_1_out), .sel(shouldStall2));  // open: en
  Adder #(.width(32)) adder_1 (.a(multiplexer_1_out), .b(prev_val), .out(Product));  // open: cin, cout
  Register #(.width(32)) register_3 (.D(Product), .Q(prev_val), .clk(Clock), .clr(Mul_Div_Reset));  // open: en
  Comparator #(.width(32), .mode("unsigned")) comparator_1 (
    .a(y_reg), .b(ctr), .gt(shouldStall2), .eq(shouldStall1));  // open: lt
  or or_1 (Stall_Pipeline, shouldStall2, shouldStall1);
  // Probe on Product

  // Other names for the same wires on the sheet: clk = Clock; rst = Mul_Div_Reset; shouldStall = Stall_Pipeline
endmodule

// 31
module DIVSUB (
  input  [31:0] X,
  input  [31:0] Y,
  input  Clock,
  input  Mul_Div_Reset,
  output Stall_Pipeline,
  output [31:0] toHi,
  output [31:0] Division
);

  wire barrow_out, comparator_2_eq, comparator_3_gt, infinity, shouldStall, stall, stall_breaker, use_x_reg;
  wire [31:0] ctr, pick_ctr, prev_val, Quotient, stall_ctr, x_prime__reg, x_reg, y_reg;

  // Probe on X
  // Probe on Y
  Counter #(.width(32), .max('hffffffff)) counter_1 (
    .Q(stall_ctr), .clk(Clock), .clr(Mul_Div_Reset));  // open: load, D, count, carry
  Register #(.width(32)) register_1 (.D(X), .en(Mul_Div_Reset), .Q(x_reg), .clk(Clock));  // open: clr
  Register #(.width(32)) register_2 (.D(Y), .en(Mul_Div_Reset), .Q(y_reg), .clk(Clock));  // open: clr
  Comparator #(.width(32), .mode("unsigned")) comparator_1 (
    .a(pick_ctr), .b({32{1'b0}}), .eq(use_x_reg));  // open: gt, lt
  Counter #(.width(32), .max('hffffffff)) counter_2 (
    .count(shouldStall), .Q(pick_ctr), .clk(Clock), .clr(Mul_Div_Reset));  // open: load, D, carry
  Multiplexer #(.width(32)) multiplexer_1 (
    .in0(prev_val), .in1(x_reg), .out(x_prime__reg), .sel(use_x_reg));  // open: en
  Subtractor #(.width(32)) subtractor_1 (.a(x_prime__reg), .b(y_reg), .out(Quotient), .bout(barrow_out));  // open: bin
  Comparator #(.width(32), .mode("unsigned")) comparator_2 (
    .a(y_reg), .b({32{1'b0}}), .eq(comparator_2_eq));  // open: gt, lt
  Comparator #(.width(32), .mode("unsigned")) comparator_3 (
    .a(stall_ctr), .b(32'h2), .gt(comparator_3_gt));  // open: eq, lt
  Comparator #(.width(32), .mode("unsigned")) comparator_4 (
    .a(stall_ctr), .b({32{1'b0}}), .eq(stall_breaker));  // open: gt, lt
  // Probe on x_prime__reg
  Register #(.width(32)) register_3 (.D(Quotient), .en(shouldStall), .Q(prev_val), .clk(Clock), .clr(Mul_Div_Reset));
  and and_1 (infinity, comparator_2_eq, comparator_3_gt);
  not not_1 (shouldStall, barrow_out);
  Multiplexer multiplexer_2 (.in0(stall), .in1(1'b0), .out(Stall_Pipeline), .sel(infinity));  // open: en
  Multiplexer #(.width(32)) multiplexer_3 (
    .in0(x_prime__reg), .in1({32{1'b1}}), .out(toHi), .sel(infinity));  // open: en
  Multiplexer #(.width(32)) multiplexer_4 (.in0(ctr), .in1({32{1'b1}}), .out(Division), .sel(infinity));  // open: en
  or or_1 (stall, shouldStall, stall_breaker);
  Counter #(.width(32), .max('hffffffff)) counter_3 (
    .count(shouldStall), .Q(ctr), .clk(Clock), .clr(Mul_Div_Reset));  // open: load, D, carry
  // Probe on Division

  // Other names for the same wires on the sheet: clk = Clock; final_ctr[31:0] = Division;
  //   final_stall = Stall_Pipeline; final_x_prime__reg[31:0] = toHi; rst = Mul_Div_Reset
endmodule

module ffs (
  input  [31:0] X,
  input  [31:0] Y,
  input  Clock,
  input  Mul_Div_Reset,
  output Stall_Pipeline,
  output [31:0] toHi,
  output [31:0] Division
);

  wire barrow_out, counter_1_q, not_1_out, use_x_reg;
  wire [31:0] pick_ctr, prev_val, Quotient, x_reg, y_reg;

  Register #(.width(32)) register_1 (.D(X), .en(Mul_Div_Reset), .Q(x_reg), .clk(Clock));  // open: clr
  Register #(.width(32)) register_2 (.D(Y), .en(Mul_Div_Reset), .Q(y_reg), .clk(Clock));  // open: clr
  Register #(.width(32)) register_3 (.D(Quotient), .en(Stall_Pipeline), .Q(prev_val), .clk(Clock), .clr(Mul_Div_Reset));
  Counter #(.width(1), .max('h1)) counter_1 (
    .count(not_1_out), .Q(counter_1_q), .clk(barrow_out), .clr(Mul_Div_Reset));  // open: load, D, carry
  not not_1 (not_1_out, Mul_Div_Reset);
  Multiplexer #(.width(32)) multiplexer_1 (.in0(prev_val), .in1(x_reg), .out(toHi), .sel(use_x_reg));  // open: en
  // Probe on toHi
  not not_2 (Stall_Pipeline, counter_1_q);
  Comparator #(.width(32), .mode("unsigned")) comparator_1 (
    .a(pick_ctr), .b({32{1'b0}}), .eq(use_x_reg));  // open: gt, lt
  Subtractor #(.width(32)) subtractor_1 (.a(toHi), .b(y_reg), .out(Quotient), .bout(barrow_out));  // open: bin
  // Probe on Division
  Counter #(.width(32), .max('hffffffff)) counter_2 (
    .count(Stall_Pipeline), .Q(Division), .clk(Clock), .clr(Mul_Div_Reset));  // open: load, D, carry
  Counter #(.width(32), .max('hffffffff)) counter_3 (
    .count(Stall_Pipeline), .Q(pick_ctr), .clk(Clock), .clr(Mul_Div_Reset));  // open: load, D, carry
  // Probe on X
  // Probe on Y

  // Other names for the same wires on the sheet: clk = Clock; ctr[31:0] = Division; rst = Mul_Div_Reset;
  //   shouldStall = Stall_Pipeline; x_prime__reg[31:0] = toHi
endmodule
