// Logisim project cpu.circ as structural Verilog: 4 circuits, main circuit main
module main (
  input  [31:0] RS_READ_VALUE,
  input  [31:0] RT_READ_VALUE,
  input  [31:0] INSTRUCTION,
  input  CLOCK,
  input  RESET,
  output [31:0] Lo,
  output [31:0] Hi,
  output [31:0] t0,
  output [31:0] t1,
  output [31:0] t2,
  output [31:0] t3,
  output [4:0] RS,
  output [4:0] RT,
  output [4:0] Write_Register,
  output [31:0] RD_WRITE_VALUE,
  output RD_WRITE_ENABLE,
  output [23:0] FETCH_ADDRESS
);

  wire MEM_p1, MEM_p2;

  // regfile_main RegFile: pin names not known
  // alu_main ALU: pin names not known
  // mem_main MEM: pin names not known; wires that end beside it: MEM_p1, MEM_p2, MEM_p2

  // Other names for the same wires on the sheet: clk = CLOCK; RS_VAL[31:0] = RS_READ_VALUE; rst = RESET;
  //   RT_VAL[31:0] = RT_READ_VALUE

  // Notes on the sheet:
  //   These are outputs/inputs from run.circ
  //   These are outputs to run.circ
  //   Feel free to move these
endmodule

module control (
  input  [5:0] OPCODE,
  input  [5:0] FUNCT,
  input  Stalling,
  input  Equals,
  output [5:0] ALU_select,
  output imm,
  output pc_selector,
  output Data_Write,
  output Reg_Write,
  output Reg_Dest,
  output Ext_Select,
  output \byte ,
  output load_mem,
  output shift,
  output Mul_Div_Reset,
  output mfhi,
  output mflo
);

  wire addiu, and_2_out, and_3_out, and_8_out, andi, beq, bne, comparator_7_eq, comparator_9_eq,
       comparator_12_eq, comparator_13_eq, comparator_14_eq, comparator_15_eq, comparator_16_eq,
       comparator_18_eq, comparator_19_eq, comparator_20_eq, comparator_21_eq, comparator_22_eq,
       comparator_23_eq, comparator_24_eq, comparator_25_eq, comparator_26_lt, comparator_27_eq, data,
       don_t_write____mul_div, imm_select, j, jr, lui, not_1_out, not_2_out, not_store, or_1_out, or_2_out,
       or_3_out, or_5_out, or_6_out, ori, r_type, shift_t;
  wire [5:0] multiplexer_1_out, multiplexer_2_out, multiplexer_3_out, multiplexer_4_out;

  Comparator #(.width(6), .mode("unsigned")) comparator_1 (.a(OPCODE), .b({6{1'b0}}), .eq(r_type));  // open: gt, lt
  Comparator #(.width(6), .mode("unsigned")) comparator_2 (.a(OPCODE), .b(6'b001001), .eq(addiu));  // open: gt, lt
  Comparator #(.width(6), .mode("unsigned")) comparator_3 (.a(OPCODE), .b(6'b001101), .eq(ori));  // open: gt, lt
  Comparator #(.width(6), .mode("unsigned")) comparator_4 (.a(OPCODE), .b(6'b001111), .eq(lui));  // open: gt, lt
  Comparator #(.width(6), .mode("unsigned")) comparator_5 (.a(OPCODE), .b(6'b011111), .gt(data));  // open: eq, lt
  Comparator #(.width(6), .mode("unsigned")) comparator_6 (.a(OPCODE), .b(6'b001100), .eq(andi));  // open: gt, lt
  Comparator #(.width(6), .mode("unsigned")) comparator_7 (
    .a(FUNCT), .b(6'b001000), .eq(comparator_7_eq));  // open: gt, lt
  Comparator #(.width(6), .mode("unsigned")) comparator_8 (.a(OPCODE), .b(6'b000010), .eq(j));  // open: gt, lt
  Comparator #(.width(6), .mode("unsigned")) comparator_9 (
    .a(OPCODE), .b(6'b000011), .eq(comparator_9_eq));  // open: gt, lt
  Comparator #(.width(6), .mode("unsigned")) comparator_10 (.a(OPCODE), .b(6'b000100), .eq(beq));  // open: gt, lt
  Comparator #(.width(6), .mode("unsigned")) comparator_11 (.a(OPCODE), .b(6'b000101), .eq(bne));  // open: gt, lt
  not not_1 (not_1_out, Equals);
  and and_1 (jr, r_type, comparator_7_eq);
  and and_2 (and_2_out, beq, Equals);
  and and_3 (and_3_out, bne, not_1_out);
  Comparator #(.width(6), .mode("unsigned")) comparator_12 (
    .a(6'b111110), .b(FUNCT), .eq(comparator_12_eq));  // open: gt, lt
  Comparator #(.width(6), .mode("unsigned")) comparator_13 (
    .a(FUNCT), .b({6{1'b1}}), .eq(comparator_13_eq));  // open: gt, lt
  Multiplexer #(.width(6), .enable("false")) multiplexer_1 (
    .in0({6{1'b0}}), .in1(FUNCT), .out(multiplexer_1_out), .sel(r_type));
  or or_1 (or_1_out, comparator_12_eq, comparator_13_eq);
  not not_2 (not_2_out, Stalling);
  Multiplexer #(.width(6), .enable("false")) multiplexer_2 (
    .in0(multiplexer_1_out), .in1(6'b100001), .out(multiplexer_2_out), .sel(or_2_out));
  or or_2 (or_2_out, addiu, data);
  Comparator #(.width(6), .mode("unsigned")) comparator_14 (
    .a(OPCODE), .b({6{1'b0}}), .eq(comparator_14_eq));  // open: gt, lt
  Comparator #(.width(6), .mode("unsigned")) comparator_15 (
    .a(OPCODE), .b(6'b000100), .eq(comparator_15_eq));  // open: gt, lt
  Comparator #(.width(6), .mode("unsigned")) comparator_16 (
    .a(OPCODE), .b(6'b000101), .eq(comparator_16_eq));  // open: gt, lt
  and and_4 (Mul_Div_Reset, r_type, or_1_out, not_2_out);
  Multiplexer #(.width(6), .enable("false")) multiplexer_3 (
    .in0(multiplexer_2_out), .in1(6'b100101), .out(multiplexer_3_out), .sel(ori));
  or or_3 (or_3_out, comparator_14_eq, comparator_15_eq, comparator_16_eq);
  or or_4 (pc_selector, jr, j, comparator_9_eq, and_2_out, and_3_out);
  Multiplexer #(.width(6), .enable("false")) multiplexer_4 (
    .in0(multiplexer_3_out), .in1({6{1'b0}}), .out(multiplexer_4_out), .sel(lui));
  not not_3 (imm_select, or_3_out);
  Multiplexer #(.width(6), .enable("false")) multiplexer_5 (
    .in0(multiplexer_4_out), .in1(6'b100100), .out(ALU_select), .sel(andi));
  Comparator #(.width(6), .mode("unsigned")) comparator_17 (
    .a(OPCODE), .b(6'b100111), .gt(Data_Write), .lt(not_store));  // open: eq
  Comparator #(.width(6), .mode("unsigned")) comparator_18 (
    .a(FUNCT), .b(6'b111110), .eq(comparator_18_eq));  // open: gt, lt
  or or_5 (or_5_out, jr, j, beq, bne, Data_Write, Stalling);
  Comparator #(.width(6), .mode("unsigned")) comparator_19 (
    .a(FUNCT), .b(6'b010010), .eq(comparator_19_eq));  // open: gt, lt
  Comparator #(.width(6), .mode("unsigned")) comparator_20 (
    .a(FUNCT), .b(6'b010000), .eq(comparator_20_eq));  // open: gt, lt
  Comparator #(.width(6), .mode("unsigned")) comparator_21 (
    .a(OPCODE), .b(6'b001101), .eq(comparator_21_eq));  // open: gt, lt
  Comparator #(.width(6), .mode("unsigned")) comparator_22 (
    .a(OPCODE), .b(6'b001100), .eq(comparator_22_eq));  // open: gt, lt
  Comparator #(.width(6), .mode("unsigned")) comparator_23 (
    .a(OPCODE), .b(6'b100100), .eq(comparator_23_eq));  // open: gt, lt
  Comparator #(.width(6), .mode("unsigned")) comparator_24 (
    .a(OPCODE), .b(6'b100000), .eq(comparator_24_eq));  // open: gt, lt
  Comparator #(.width(6), .mode("unsigned")) comparator_25 (
    .a(FUNCT), .b({6{1'b0}}), .eq(comparator_25_eq));  // open: gt, lt
  Comparator #(.width(6), .mode("unsigned")) comparator_26 (
    .a(FUNCT), .b(6'b000100), .lt(comparator_26_lt));  // open: gt, eq
  Comparator #(.width(6), .mode("unsigned")) comparator_27 (
    .a(FUNCT), .b({6{1'b1}}), .eq(comparator_27_eq));  // open: gt, lt
  or or_6 (or_6_out, comparator_27_eq, comparator_18_eq);
  not not_4 (Reg_Write, or_5_out);
  and and_5 (mflo, comparator_19_eq, r_type);
  and and_6 (mfhi, r_type, comparator_20_eq);
  or or_7 (Ext_Select, comparator_21_eq, comparator_22_eq);
  or or_8 (\byte , comparator_23_eq, comparator_24_eq);
  or or_9 (shift_t, comparator_25_eq, comparator_26_lt);
  and and_7 (don_t_write____mul_div, r_type, or_6_out);
  and and_8 (and_8_out, shift_t, r_type);
  or or_10 (imm, imm_select, and_8_out);
  not not_5 (Reg_Dest, r_type);
  and and_9 (load_mem, data, not_store);
  and and_10 (shift, shift_t, r_type);

  // Other names for the same wires on the sheet: Eq = Equals; pc_select = pc_selector; Stall = Stalling
endmodule

module t0__t3 (
  input  [4:0] register,
  output \output 
);

  wire not_1_out, not_2_out;

  not not_1 (not_1_out, register[2]);
  not not_2 (not_2_out, register[4]);
  and and_1 (\output , not_1_out, register[3], not_2_out);
endmodule

module new_pc (
  input  [15:0] Immediate,
  input  [23:0] address,
  input  [23:0] Program_Counter,
  input  [5:0] opcode,
  output [23:0] Addess
);

  wire beq, bne, branch;
  wire [23:0] adder_1_out, bit_extender_1_out, branch_addr, subtractor_1_out;

  Comparator #(.width(6), .mode("unsigned")) comparator_1 (.a(opcode), .b(6'b000100), .eq(beq));  // open: gt, lt
  Comparator #(.width(6), .mode("unsigned")) comparator_2 (.a(opcode), .b(6'b000101), .eq(bne));  // open: gt, lt
  assign bit_extender_1_out = {{8{Immediate[15]}}, Immediate};  // Bit_Extender bit_extender_1
  Adder #(.width(24)) adder_1 (.a(bit_extender_1_out), .b(Program_Counter), .out(adder_1_out));  // open: cin, cout
  Subtractor #(.width(24)) subtractor_1 (.a(address), .b(24'h100000), .out(subtractor_1_out));  // open: bin, bout
  or or_1 (branch, beq, bne);
  Adder #(.width(24)) adder_2 (.a(adder_1_out), .b(24'h1), .out(branch_addr));  // open: cin, cout
  Multiplexer #(.width(24), .enable("false")) multiplexer_1 (
    .in0(subtractor_1_out), .in1(branch_addr), .out(Addess), .sel(branch));

  // Other names for the same wires on the sheet: addr[23:0] = address; imm[15:0] = Immediate;
  //   PC[23:0] = Program_Counter
endmodule
