// Logisim project regfile.circ as structural Verilog: 1 circuit, main circuit main
module main (
  input  [1:0] Read_register_1,
  input  [1:0] Read_register_2,
  input  [1:0] write_register,
  input  [31:0] write_data,
  input  RegWrite,
  input  clock,
  output [31:0] t0_Value,
  output [31:0] t1_Value,
  output [31:0] t2_Value,
  output [31:0] t3_Value,
  output [31:0] Read_Data_1,
  output [31:0] Read_Data_2
);

  wire decoder_1_out0, decoder_1_out1, decoder_1_out2, decoder_1_out3, ealt0, ealt1, ealt2, ealt3;

  // NOT_Gate not_1 is placed but not wired
  and and_1 (ealt0, RegWrite, decoder_1_out0);
  Decoder #(.select(2)) decoder_1 (
    .out0(decoder_1_out0), .out1(decoder_1_out1), .out2(decoder_1_out2), .out3(decoder_1_out3),
    .sel(write_register));  // open: en
  Register #(.width(32)) t0 (.D(write_data), .en(ealt0), .Q(t0_Value), .clk(clock));  // open: clr
  Register #(.width(32)) t1 (.D(write_data), .en(ealt1), .Q(t1_Value), .clk(clock));  // open: clr
  Register #(.width(32)) t2 (.D(write_data), .en(ealt2), .Q(t2_Value), .clk(clock));  // open: clr
  Register #(.width(32)) t3 (.D(write_data), .en(ealt3), .Q(t3_Value), .clk(clock));  // open: clr
  and and_2 (ealt1, RegWrite, decoder_1_out1);
  and and_3 (ealt2, RegWrite, decoder_1_out2);
  and and_4 (ealt3, RegWrite, decoder_1_out3);
  Multiplexer #(.select(2), .width(32)) multiplexer_1 (
    .in0(t0_Value), .in1(t1_Value), .in2(t2_Value), .in3(t3_Value), .out(Read_Data_1), .sel(Read_register_1));  // open: en
  Multiplexer #(.select(2), .width(32)) multiplexer_2 (
    .in0(t0_Value), .in1(t1_Value), .in2(t2_Value), .in3(t3_Value), .out(Read_Data_2), .sel(Read_register_2));  // open: en

  // Other names for the same wires on the sheet: clk = clock; RD1[31:0] = Read_Data_1; RD2[31:0] = Read_Data_2;
  //   Rr1[1:0] = Read_register_1; Rr2[1:0] = Read_register_2; RW = RegWrite; t0V[31:0] = t0_Value;
  //   t1V[31:0] = t1_Value; t2V[31:0] = t2_Value; t3V[31:0] = t3_Value; WD[31:0] = write_data;
  //   Wr[1:0] = write_register

  // Notes on the sheet:
  //   These are INPUTS to the circuit
  //   These are INPUTS to the circuit
  //   Yet again, the clock is not an actual clock, but an input, one that will be driven from a higher circuit
  //   DO NOT CHANGE THE LOCATIONS OF THE INPUTS/OUTPUTS! IF YOU DO SO, YOU NEED TO MAKE SURE THE PINS ARE AT THE RIGHT PLACE!
  //   These are OUTPUTS to the circuit
  //   These are OUTPUTS to the circuit
endmodule
